# Fritzing sketch Camera V2 (saved by Fritzing 1.0.2b)
breadboards: 1

parts:
  Raspberry_Pi_1 = Raspberry Pi 3 [part_number=RPI-3-V1.2]
  R2 = Resistor [tolerance=±5% power=0.25W resistance=220 package=THT]
  DS1 = DS18B20 1-Wire Temperature Sensor Probe
  U1 = TRANSCHIPTC5747 [package=camera_sfv24r-2st_2]  # not connected

nets:
  3V3: Raspberry_Pi_1.3v3, R2.Pin_1, DS1.VDD
  N1: Raspberry_Pi_1.GPIO4, R2.Pin_0, DS1.DQ
  GND: Raspberry_Pi_1.GND, DS1.GND

notes:
  Light goes here
  USB POWERED
